// Logisim project practial1.circ as structural Verilog: 1 circuit, main circuit main
module main (
  input  in_1,
  input  in_2,
  input  in_3,
  input  in_4,
  output out_5,
  output out_6
);

  wire and_1_out, not_1_out, not_2_out;

  not not_1 (not_1_out, in_3);
  not not_2 (not_2_out, in_4);
  not not_3 (out_5, and_1_out);
  and and_1 (and_1_out, in_1, in_2);
  or or_1 (out_6, not_1_out, not_2_out);

  // Notes on the sheet:
  //   LHS:
  //   RHS:
  //   1
endmodule
